// Logisim project webb_hw2.circ as structural Verilog: 2 circuits, main circuit full_adder_Jeremiah_Webb
module full_adder_Jeremiah_Webb (
  input  A,
  input  B,
  input  Cin,
  output Sum,
  output Cout
);

  wire and_1_out, and_2_out, xor_1_out;

  xor xor_1 (xor_1_out, A, B);
  and and_1 (and_1_out, A, B);
  xor xor_2 (Sum, xor_1_out, Cin);
  and and_2 (and_2_out, Cin, xor_1_out);
  or or_1 (Cout, and_2_out, and_1_out);
endmodule

module ripplecarryadder_Jeremiah_Webb (
  input  in_1,
  input  [5:0] in_2,
  input  [5:0] in_3,
  output [5:0] Sum,
  output Overflow
);

  wire full_adder_jeremiah_webb_1_cout, full_adder_jeremiah_webb_2_cout, full_adder_jeremiah_webb_3_cout,
       full_adder_jeremiah_webb_4_cout, full_adder_jeremiah_webb_5_cout, not_1_out;

  not not_1 (not_1_out, in_1);
  full_adder_Jeremiah_Webb full_adder_jeremiah_webb_1 (
    .A(in_2[0]), .B(in_3[0]), .Cin(not_1_out), .Sum(Sum[0]), .Cout(full_adder_jeremiah_webb_1_cout));
  full_adder_Jeremiah_Webb full_adder_jeremiah_webb_2 (
    .A(in_2[5]), .B(in_3[1]), .Cin(full_adder_jeremiah_webb_1_cout), .Sum(Sum[1]),
    .Cout(full_adder_jeremiah_webb_2_cout));
  full_adder_Jeremiah_Webb full_adder_jeremiah_webb_3 (
    .A(in_2[2]), .B(in_3[2]), .Cin(full_adder_jeremiah_webb_2_cout), .Sum(Sum[2]),
    .Cout(full_adder_jeremiah_webb_3_cout));
  full_adder_Jeremiah_Webb full_adder_jeremiah_webb_4 (
    .A(in_2[3]), .B(in_3[3]), .Cin(full_adder_jeremiah_webb_3_cout), .Sum(Sum[3]),
    .Cout(full_adder_jeremiah_webb_4_cout));
  full_adder_Jeremiah_Webb full_adder_jeremiah_webb_5 (
    .A(in_2[4]), .B(in_3[4]), .Cin(full_adder_jeremiah_webb_4_cout), .Sum(Sum[4]),
    .Cout(full_adder_jeremiah_webb_5_cout));
  full_adder_Jeremiah_Webb full_adder_jeremiah_webb_6 (
    .A(in_2[5]), .B(in_3[5]), .Cin(full_adder_jeremiah_webb_5_cout), .Sum(Sum[5]), .Cout(Overflow));

  assign in_2[1] = in_2[5];
endmodule
